// Digital circuit ALU.dig as structural Verilog
module ALU (
  input  [15:0] A,
  input  [15:0] B,
  input  C_i,
  input  [4:0] Sel,
  output [15:0] Sum,
  output C_o,
  output E,
  output N
);

  wire _74181_1_p20, _74181_1_p21, _74181_2_p21, _74181_2_p22, _74181_3_p21, _74181_3_p22, _74181_4_p22;

  // _74181 _74181_1: pin names not known; wires that end beside it: C_i, A[0], A[1], A[2], A[3], B[0], B[1], B[2], B[3], Sel[0], Sel[1], Sel[2], Sel[3], Sel[4], 1'b1, Sum[0], Sum[1], Sum[2], Sum[3], _74181_1_p20, _74181_1_p21
  // _74181 _74181_2: pin names not known; wires that end beside it: 1'b0, _74181_1_p21, A[4], A[5], A[6], A[7], B[4], B[5], B[6], B[7], Sel[0], Sel[1], Sel[2], Sel[3], Sel[4], 1'b1, Sum[4], Sum[5], Sum[6], Sum[7], _74181_2_p21, _74181_2_p22
  // _74181 _74181_3: pin names not known; wires that end beside it: 1'b0, _74181_2_p22, A[8], A[9], A[10], A[11], B[8], B[9], B[10], B[11], Sel[0], Sel[1], Sel[2], Sel[3], Sel[4], 1'b1, Sum[8], Sum[9], Sum[10], Sum[11], _74181_3_p21, _74181_3_p22
  // _74181 _74181_4: pin names not known; wires that end beside it: 1'b0, _74181_3_p22, A[12], A[13], A[14], A[15], B[12], B[13], B[14], B[15], Sel[0], Sel[1], Sel[2], Sel[3], Sel[4], 1'b1, 1'b0, Sum[12], Sum[13], Sum[14], N, _74181_4_p22, C_o
  and and_1 (E, _74181_1_p20, _74181_2_p21, _74181_3_p21, _74181_4_p22);

  assign Sum[15] = N;
endmodule
