// Digital circuit ALU_LAYOUT.dig as structural Verilog
module ALU_LAYOUT (
);

  // _74245 _74245_1: pin names not known
  // _74151 _74151_1: pin names not known
  // _74138 _74138_1: pin names not known
  // _74138 _74138_2: pin names not known
  // _74245 _74245_2: pin names not known
  // _74245 _74245_3: pin names not known
  // _74182 _74182_1: pin names not known
  // _74138 _74138_3: pin names not known
  // _74245 _74245_4: pin names not known
  // _74245 _74245_5: pin names not known
  // _74670 _74670_1: pin names not known
  // _74670 _74670_2: pin names not known
  // _74670 _74670_3: pin names not known
  // _74670 _74670_4: pin names not known
  // _74245 _74245_6: pin names not known
  // _74670 _74670_5: pin names not known
  // _74670 _74670_6: pin names not known
  // _74670 _74670_7: pin names not known
  // _74670 _74670_8: pin names not known
  // _74181 _74181_1: pin names not known
  // _74670 _74670_9: pin names not known
  // _74670 _74670_10: pin names not known
  // _74670 _74670_11: pin names not known
  // _74670 _74670_12: pin names not known
  // _74670 _74670_13: pin names not known
  // _74670 _74670_14: pin names not known
  // _74670 _74670_15: pin names not known
  // _74670 _74670_16: pin names not known
  // _74181 _74181_2: pin names not known
  // _74670 _74670_17: pin names not known
  // _74670 _74670_18: pin names not known
  // _74670 _74670_19: pin names not known
  // _74670 _74670_20: pin names not known
  // _74181 _74181_3: pin names not known
  // _74670 _74670_21: pin names not known
  // _74670 _74670_22: pin names not known
  // _74670 _74670_23: pin names not known
  // _74670 _74670_24: pin names not known
  // _74670 _74670_25: pin names not known
  // _74670 _74670_26: pin names not known
  // _74670 _74670_27: pin names not known
  // _74670 _74670_28: pin names not known
  // _74181 _74181_4: pin names not known
  // _74670 _74670_29: pin names not known
  // _74670 _74670_30: pin names not known
  // _74670 _74670_31: pin names not known
  // _74670 _74670_32: pin names not known

  // Notes on the sheet:
  //   50
  //   45
  //   40
  //   35
  //   30
  //   25
  //   20
  //   15
  //   10
  //   1
  //   W
  //   V
  //   U
  //   T
  //   S
  //   R
  //   P
  //   N
  //   M
  //   L
  //   K
  //   J
  //   H
  //   G
  //   F
  //   E
  //   D
  //   C
  //   B
  //   A
endmodule
