// Logisim project CPU.circ as structural Verilog: 1 circuit, main circuit main
module main (
);

  wire AW, BW, CW, ROUT;
  wire [2:0] OP1;
  wire [15:0] A_q, adder_1_out, and_1_out, B_q, C_q, DBUS, LBUS, MDR_q, MOUT, not_1_out, or_1_out, RBUS,
       shifter_1_out, subtractor_1_out, xor_1_out;

  Register #(.width(16)) MDR (.D(LBUS), .Q(MDR_q));  // open: en, clk, clr
  Adder #(.width(16)) adder_1 (.a(RBUS), .b(MDR_q), .out(adder_1_out));  // open: cin, cout
  Subtractor #(.width(16)) subtractor_1 (.a(RBUS), .b(MDR_q), .out(subtractor_1_out));  // open: bin, bout
  assign not_1_out = ~RBUS;  // NOT_Gate not_1, 16 bits wide
  assign and_1_out = RBUS & MDR_q;  // AND_Gate and_1, 16 bits wide
  assign or_1_out = RBUS | MDR_q;  // OR_Gate or_1, 16 bits wide
  assign xor_1_out = RBUS ^ MDR_q;  // XOR_Gate xor_1, 16 bits wide
  Shifter #(.width(16)) shifter_1 (.in(RBUS), .\dist (4'b1111), .out(shifter_1_out));
  Register #(.width(16)) A (.D(DBUS), .en(AW), .Q(A_q));  // open: clk, clr
  Register #(.width(16)) B (.D(DBUS), .en(BW), .Q(B_q));  // open: clk, clr
  Register #(.width(16)) C (.D(DBUS), .en(CW), .Q(C_q));  // open: clk, clr
  Multiplexer #(.enable("true"), .select(3), .width(16)) multiplexer_1 (
    .in0(RBUS), .in1(adder_1_out), .in2(subtractor_1_out), .in3(not_1_out), .in4(and_1_out), .in5(or_1_out),
    .in6(xor_1_out), .in7(shifter_1_out), .out(DBUS), .sel(OP1), .en(ROUT));
  Multiplexer #(.select(2), .width(16)) multiplexer_2 (.in0(A_q), .in1(B_q), .in2(C_q), .out(RBUS));  // open: in3, sel
  RAM #(.addrWidth(16), .dataWidth(16)) ram_1 (.dout(MOUT));  // open: addr, we, oe, clk, din
endmodule
