// Digital circuit CPU.dig as structural Verilog
module CPU (
  input  clk,
  output out_2
);

  wire and_2_out, and_3_out, BRA, C, C_SEL, C_VAL, demultiplexer_2_out_0, demultiplexer_2_out_1,
       demultiplexer_2_out_2, demultiplexer_2_out_3, demultiplexer_2_out_4, demultiplexer_3_out_0,
       demultiplexer_3_out_1, demultiplexer_3_out_2, demultiplexer_3_out_3, demultiplexer_3_out_4,
       demultiplexer_4_out_0, demultiplexer_4_out_1, demultiplexer_4_out_2, multiplexer_3_out,
       multiplexer_4_out, nALU, nALU_RD, nBANK_WR, nCOND_OUT, nFLAG_WR, nIMM, nMEM_RD, nMEM_WR, nMOV,
       not_1_out, not_2_out, not_3_out, not_4_out, not_10_out, not_16_out, nPC_RD, nPC_WR, nREG_WR, nSTAT_RD,
       nSTAT_WR, nSWP_RD, or_2_out, or_3_out, xor_1_out;
  wire [1:0] OP1;
  wire [2:0] FLAGS, pulldown_4_out, pulldown_8_out;
  wire [2:2] and_1_out, undriven_2;
  wire [3:0] driverinvsel_5_out, FLAG_da, REG_DEST, REG_SRC;
  wire [4:0] ALU_OP;
  wire [5:0] OP2;
  wire [7:0] driverinvsel_6_out, IMM_HI_q;
  wire [9:0] driverinvsel_1_out;
  wire [10:10] undriven;
  wire [15:0] add_1_s, alu_1_sum, bitextender_1_out, L_BUS, multiplexer_1_out, PC_da, R_BUS, REG_da, REG_db;
  wire [15:14] multiplexer_2_out;
  wire [17:0] A_BUS;

  Multiplexer #(.Bits(16)) multiplexer_1 (.sel(nPC_WR), .in_0(R_BUS), .in_1(add_1_s), .out(multiplexer_1_out));
  RegisterFile #(.AddrBits(4), .Bits(16)) REG (
    .Din(R_BUS), .we(not_1_out), .Rw(REG_DEST), .C(clk), .Ra(REG_SRC), .Rb(REG_DEST), .Da(REG_da), .Db(REG_db));
  not not_1 (not_1_out, nREG_WR);
  RegisterFile #(.AddrBits(1), .Bits(16)) PC (
    .Din(multiplexer_1_out), .we(1'b1), .Rw(1'b0), .C(clk), .Ra(1'b0), .Rb(1'b0), .Da(PC_da));  // open: Db
  Demultiplexer #(.Selector_Bits(2)) demultiplexer_1 (
    .sel(A_BUS[17:16]), .in(1'b1));  // open: out_0, out_1, out_2, out_3
  Add #(.Bits(16)) add_1 (.a(PC_da), .b(bitextender_1_out), .c_i(1'b1), .s(add_1_s));  // open: c_o
  BitExtender #(.inputBits(10)) bitextender_1 (.in(driverinvsel_1_out), .out(bitextender_1_out));
  or or_1 (out_2, nMEM_WR, ~nMEM_RD);  // Or
  not not_2 (not_2_out, nMEM_WR);
  and and_1 (and_1_out[2], nMEM_RD, nMEM_WR);
  assign driverinvsel_1_out = ~nCOND_OUT ? {OP2[1:0], REG_SRC, REG_DEST} : 10'bz;  // DriverInvSel driverinvsel_1
  PullDown #(.Bits(10)) pulldown_1 (.out(driverinvsel_1_out));
  assign R_BUS = ~nPC_RD ? PC_da : 16'bz;  // DriverInvSel driverinvsel_2
  Multiplexer #(.Bits(16)) multiplexer_2 (
    .sel(and_1_out[2]), .in_0(REG_da), .in_1(PC_da), .out({multiplexer_2_out, A_BUS[13:0]}));
  ROM #(.AddrBits(16), .Bits(16)) rom_1 (.A(A_BUS[15:0]), .sel(not_3_out), .D(L_BUS));
  not not_3 (not_3_out, not_2_out);
  PullDown #(.Bits(16)) pulldown_2 (.out(L_BUS));
  not not_4 (not_4_out, nBANK_WR);
  Multiplexer multiplexer_3 (.sel(C_SEL), .in_0(C_VAL), .in_1(C), .out(multiplexer_3_out));
  RegisterFile #(.AddrBits(3), .Bits(4)) BANK (
    .Din(R_BUS[3:0]), .we(not_4_out), .Rw(R_BUS[14:12]), .C(clk), .Ra({and_1_out[2], multiplexer_2_out}),
    .Rb(3'b000), .Da(A_BUS[17:14]));  // open: Db
  ALU alu_1 (
    .C_i(multiplexer_3_out), .A(REG_da), .B(REG_db), .Sel(ALU_OP), .Sum(alu_1_sum), .E(FLAGS[2]),
    .C_o(FLAGS[1]), .N(FLAGS[0]));
  assign R_BUS = ~nSWP_RD ? {alu_1_sum[7:0], alu_1_sum[15:8]} : 16'bz;  // DriverInvSel driverinvsel_3
  assign R_BUS = ~nALU_RD ? alu_1_sum : 16'bz;  // DriverInvSel driverinvsel_4
  PullDown #(.Bits(16)) pulldown_3 (.out(R_BUS));
  Demultiplexer #(.Selector_Bits(3)) demultiplexer_2 (
    .sel(pulldown_4_out), .in(nIMM), .out_0(demultiplexer_2_out_0), .out_1(demultiplexer_2_out_1),
    .out_2(demultiplexer_2_out_2), .out_3(demultiplexer_2_out_3), .out_4(demultiplexer_2_out_4));  // open: out_5, out_6, out_7
  PullDown #(.Bits(3)) pulldown_4 (.out(pulldown_4_out));
  RegisterFile #(.AddrBits(1), .Bits(3)) FLAG (
    .Din(FLAGS), .we(nFLAG_WR), .Rw(1'b0), .C(clk), .Ra(1'b0), .Rb(1'b0), .Da({C, FLAG_da[1:0]}));  // open: Db
  not not_5 (nALU_RD, demultiplexer_2_out_0);
  not not_6 (nSWP_RD, demultiplexer_2_out_1);
  not not_7 (nMEM_RD, demultiplexer_2_out_2);
  not not_8 (nSTAT_RD, demultiplexer_2_out_3);
  not not_9 (nPC_RD, demultiplexer_2_out_4);
  assign driverinvsel_5_out = ~nALU ? OP2[3:0] : 4'bz;  // DriverInvSel driverinvsel_5
  and and_2 (and_2_out, not_10_out, ~or_3_out);  // And
  assign L_BUS = and_2_out ? R_BUS : 16'bz;  // Driver driver_1
  Register #(.Bits(16)) IR (.D(L_BUS), .C(clk), .en(~1'b0), .Q({OP1, OP2, REG_SRC, REG_DEST}));
  PullDown #(.Bits(4)) pulldown_5 (.out(driverinvsel_5_out));
  ROM #(.AddrBits(4), .Bits(8)) FUNC (.A(driverinvsel_5_out), .sel(1'b1), .D({nFLAG_WR, C_VAL, C_SEL, ALU_OP}));
  Register #(.Bits(8)) IMM_HI (.D({OP2[3:0], REG_SRC}), .C(clk), .en(~nIMM), .Q(IMM_HI_q));
  assign R_BUS = and_3_out ? L_BUS : 16'bz;  // Driver driver_2
  PullDown #(.Bits(8)) pulldown_6 (.out({nFLAG_WR, C_VAL, C_SEL, ALU_OP}));
  assign driverinvsel_6_out = ~OP2[4] ? IMM_HI_q : 8'bz;  // DriverInvSel driverinvsel_6
  and and_3 (and_3_out, ~or_3_out, ~not_10_out);  // And
  or or_2 (or_2_out, nIMM, OP2[5]);
  PullDown #(.Bits(8)) pulldown_7 (.out(driverinvsel_6_out));
  not not_10 (not_10_out, nMEM_WR);
  or or_3 (or_3_out, nMEM_RD, nMEM_WR);
  Demultiplexer #(.Selector_Bits(3)) demultiplexer_3 (
    .sel(pulldown_8_out), .in(or_2_out), .out_0(demultiplexer_3_out_0), .out_1(demultiplexer_3_out_1),
    .out_2(demultiplexer_3_out_2), .out_3(demultiplexer_3_out_3), .out_4(demultiplexer_3_out_4));  // open: out_5, out_6, out_7
  PullDown #(.Bits(3)) pulldown_8 (.out(pulldown_8_out));
  assign R_BUS = ~nIMM ? {driverinvsel_6_out, OP2[3:0], REG_SRC} : 16'bz;  // DriverInvSel driverinvsel_7
  not not_11 (nREG_WR, demultiplexer_3_out_0);
  not not_12 (nBANK_WR, demultiplexer_3_out_1);
  not not_13 (nMEM_WR, demultiplexer_3_out_2);
  not not_14 (nSTAT_WR, demultiplexer_3_out_3);
  not not_15 (nPC_WR, demultiplexer_3_out_4);
  assign {pulldown_4_out, pulldown_8_out} = ~nMOV ? OP2 : 6'bz;  // DriverInvSel driverinvsel_8
  Multiplexer #(.Selector_Bits(3)) multiplexer_4 (
    .sel({undriven_2[2], OP2[4:3]}), .in_0(1'b1), .in_1(FLAG_da[0]), .in_2(not_16_out), .in_3(C),
    .in_4(FLAG_da[3]), .out(multiplexer_4_out));  // open: in_5, in_6, in_7
  not not_16 (not_16_out, FLAG_da[1]);
  xor xor_1 (xor_1_out, OP2[5], multiplexer_4_out);
  Demultiplexer #(.Selector_Bits(2)) demultiplexer_4 (
    .sel(OP1), .in(1'b1), .out_0(demultiplexer_4_out_0), .out_1(demultiplexer_4_out_1),
    .out_2(demultiplexer_4_out_2), .out_3(BRA));
  nand nand_1 (nCOND_OUT, xor_1_out, BRA);
  not not_17 (nALU, demultiplexer_4_out_0);
  not not_18 (nIMM, demultiplexer_4_out_1);
  not not_19 (nMOV, demultiplexer_4_out_2);
  // And and_4 is placed but not wired
  // Pins of 3 and 4 bits meet at {FLAG_da[3], C, FLAG_da[1:0]}
  // Pins of 10 and 11 bits meet at {undriven[10], OP2[1:0], REG_SRC, REG_DEST}
  // Pins of 2 and 3 bits meet at {undriven[10], OP2[1:0]}
  // Pins of 2 and 3 bits meet at {undriven_2[2], OP2[4:3]}

  // Notes on the sheet:
  //   contents of rom_1 (hex, n*v repeats v):
  //   0,4000,8000,c000
  //   contents of FUNC (hex, n*v repeats v):
  //   c0,0,4f,49
endmodule
