// Digital circuit CTRL_LAYOUT.dig as structural Verilog
module CTRL_LAYOUT (
);

  // _74157 _74157_1: pin names not known
  // _74157 _74157_2: pin names not known
  // _74157 _74157_3: pin names not known
  // _74157 _74157_4: pin names not known
  // _74138 _74138_1: pin names not known
  // _7408 _7408_1: pin names not known
  // _74157 _74157_5: pin names not known
  // _74377 _74377_1: pin names not known
  // _74138 _74138_2: pin names not known
  // _7404 _7404_1: pin names not known
  // _74153 _74153_1: pin names not known
  // _74377 _74377_2: pin names not known
  // _74138 _74138_3: pin names not known
  // _7486 _7486_1: pin names not known
  // _7432 _7432_1: pin names not known
  // _74670 _74670_1: pin names not known
  // _74245 _74245_1: pin names not known
  // _74245 _74245_2: pin names not known
  // _74245 _74245_3: pin names not known
  // _74283 _74283_1: pin names not known
  // _74670 _74670_2: pin names not known
  // _74157 _74157_6: pin names not known
  // _7404 _7404_2: pin names not known
  // _7404 _7404_3: pin names not known
  // _74283 _74283_2: pin names not known
  // _74670 _74670_3: pin names not known
  // _74157 _74157_7: pin names not known
  // _74175 _74175_1: pin names not known
  // _74245 _74245_4: pin names not known
  // _74283 _74283_3: pin names not known
  // _74670 _74670_4: pin names not known
  // _74157 _74157_8: pin names not known
  // _74175 _74175_2: pin names not known
  // _74245 _74245_5: pin names not known
  // _74283 _74283_4: pin names not known
  // _74670 _74670_5: pin names not known
  // _74157 _74157_9: pin names not known

  // Notes on the sheet:
  //   50
  //   45
  //   40
  //   35
  //   30
  //   25
  //   20
  //   15
  //   10
  //   1
  //   W
  //   V
  //   U
  //   T
  //   S
  //   R
  //   P
  //   IR
  //   N
  //   M
  //   L
  //   K
  //   J
  //   H
  //   PC
  //   G
  //   F
  //   E
  //   D
  //   IMM
  //   C
  //   B
  //   A
endmodule
